# Fritzing sketch final (saved by Fritzing 0.9.3b)
breadboards: 1

parts:
  부품1 = FC-28 Soil Hygrometer Module - Probe
  부품2 = FC-28 Soil Hygrometer Module
  부품3 = Arduino Uno (Rev3)
  J1 = Power Jack [package=power_jack_pth_lock]  # not connected
  VALVE1 = Plastic Solenoid Valve
  KY-1 = Keyes Relay [package=THT]
  VCC3 = Battery block 9V  # not connected
  U1 = LIPO-1000mAh [package=lipo-1000]

nets:
  N1: 부품1.POS, 부품2.POS
  N2: 부품1.NEG, 부품2.NEG
  VCC: 부품2.VCC, 부품3.5V, KY-1.power
  GND: 부품2.GND, 부품3.GND, KY-1.ground
  N3: 부품2.AO, 부품3.A0
  N4: 부품3.D8, KY-1.signal
  N5: VALVE1.no_name_yet#1, KY-1.NO
  N6: VALVE1.no_name_yet#2, U1.-
  N7: KY-1.C, U1.+

notes:
  Tροφοδοσία ηλεκτροβάνας
  12V απαιτούνται
  Tροφοδοσία Arduino. Απο εδώ παίρνουν ρεύμα και σήμα το ρελέ και ο αισθητήρας υγρασίας
  Ηλεκτροβάνα. Ανάμεσα στην τροφοδοσία και τον μικροελεγκτή, παρεμβάλλεται ο ηλεκτρονικός διακόπτης (ρελέ)
  Αισθητήρας υγρασίας εδάφους
  Breadboard
  Ηλεκτρονικός διακόπτης (ρελέ)]

custom parts:
  FC-28 Soil Hygrometer Module - Probe: The FC-28 is a soil hygrometer module that uses the Texas Instruments LM393 comparator chip to provide an analog measurement of soil humidity.
  FC-28 Soil Hygrometer Module: The FC-28 is a soil hygrometer module that uses the Texas Instruments LM393 comparator chip to provide an analog measurement of soil humidity. The digital output is high when soil moisture is over a certain threshold, as determined by adjusting the potentiometer.
  Keyes Relay: The Keyes 5V relay module is suitable for SCM development, home appliance control. It uses a 5V~12V TIL control signal which can control DC / AC signal.
