# Fritzing sketch relay_valve (saved by Fritzing 0.9.3b)

parts:
  Componente1 = Arduino Uno (Rev3)
  KY-1 = Keyes Relay [package=THT]
  VCC1 = Battery block 9V
  VALVE1 = Plastic Solenoid Valve

nets:
  N1: Componente1.D8, KY-1.signal
  N2: Componente1.5V, KY-1.power
  N3: Componente1.GND, KY-1.ground
  N4: KY-1.C, VCC1.+
  N5: KY-1.NO, VALVE1.no_name_yet

custom parts:
  Keyes Relay: The Keyes 5V relay module is suitable for SCM development, home appliance control. It uses a 5V~12V TIL control signal which can control DC / AC signal.
